// Logisim project Procesador.circ as structural Verilog: 3 circuits, main circuit main
module main (
  input  Clear,
  input  in_2
);

  wire alu_1_bitbranch, and_1_out, and_2_out, and_3_out, and_4_out, and_5_out, clock_1_out, comparator_1_eq,
       comparator_2_eq, decoder_1_out0, decoder_1_out1, decoder_1_out2, decoder_1_out3, decoder_1_out4,
       decoder_1_out5, decoder_1_out6, decoder_1_out7, decoder_1_out8, decoder_1_out9, decoder_1_out10,
       decoder_1_out11, decoder_1_out12, decoder_1_out13, decoder_1_out14, decoder_1_out15, not_1_out,
       not_2_out, not_3_out, or_1_out, or_3_out, or_4_out, or_5_out;
  wire [2:0] bitselector_3_out;
  wire [3:0] bitselector_4_out, bitselector_5_out, bitselector_6_out, bitselector_7_out;
  wire [6:0] bitselector_1_out, keyboard_1_data;
  wire [15:0] adder_1_out, alu_1_out, bitselector_2_out, bitselector_8_out, bitselector_9_out,
       controlled_buffer_1_out, multiplexer_1_out, multiplexer_2_out, multiplexer_3_out, multiplexer_4_out,
       multiplexer_5_out, or_2_out, register_1_q, regs_1_rsrc1, regs_1_rsrc2, rom_1_data, shifter_1_out,
       shifter_2_out;

  Multiplexer #(.width(16)) multiplexer_1 (
    .in0(16'h1), .in1(or_2_out), .out(multiplexer_1_out), .sel(and_5_out));  // open: en
  and and_1 (and_1_out, in_2, clock_1_out);
  Adder #(.width(16)) adder_1 (.a(register_1_q), .b(multiplexer_1_out), .out(adder_1_out));  // open: cin, cout
  Multiplexer #(.width(16)) multiplexer_2 (
    .in0(adder_1_out), .in1(or_2_out), .out(multiplexer_2_out), .sel(decoder_1_out12));  // open: en
  Clock clock_1 (.out(clock_1_out));
  Multiplexer #(.width(16)) multiplexer_3 (
    .in0(multiplexer_2_out), .in1(regs_1_rsrc1), .out(multiplexer_3_out), .sel(decoder_1_out14));  // open: en
  REGS regs_1 (
    .sRd(bitselector_6_out), .sRs1(bitselector_5_out), .sRs2(bitselector_7_out), .Reloj(not_1_out),
    .Clear(Clear), .Rdest(multiplexer_4_out), .Rsrc1(regs_1_rsrc1), .Rsrc2(regs_1_rsrc2));  // open: Enable
  not not_1 (not_1_out, and_1_out);
  Register #(.width(16)) register_1 (
    .D(multiplexer_3_out), .Q(register_1_q), .clk(and_1_out), .clr(Clear));  // open: en
  ALU alu_1 (
    .A(regs_1_rsrc1), .B(regs_1_rsrc2), .S(bitselector_3_out), .Reloj(not_1_out), .OUT(alu_1_out),
    .BitBranch(alu_1_bitbranch));
  assign controlled_buffer_1_out = decoder_1_out8 ? regs_1_rsrc2 : 16'bz;  // Controlled_Buffer controlled_buffer_1
  and and_2 (and_2_out, not_2_out, or_1_out);
  BitSelector #(.width(16), .group(7)) bitselector_1 (.in(regs_1_rsrc2), .out(bitselector_1_out), .sel(2'b00));
  not not_2 (not_2_out, and_3_out);
  and and_3 (and_3_out, decoder_1_out8, comparator_1_eq);
  Comparator #(.width(16), .mode("unsigned")) comparator_1 (
    .a(regs_1_rsrc1), .b({16{1'b1}}), .eq(comparator_1_eq));  // open: gt, lt
  Comparator #(.width(16), .mode("unsigned")) comparator_2 (
    .a(regs_1_rsrc1), .b(16'hfffe), .eq(comparator_2_eq));  // open: gt, lt
  and and_4 (and_4_out, decoder_1_out9, comparator_2_eq);
  RAM #(.addrWidth(16), .dataWidth(16)) ram_1 (
    .addr(regs_1_rsrc1), .data(controlled_buffer_1_out), .sel(and_2_out), .clk(and_1_out), .ld(not_3_out),
    .clr(Clear));
  ROM #(.addrWidth(16), .dataWidth(16)) rom_1 (.addr(register_1_q), .data(rom_1_data));  // open: sel
  Multiplexer #(.select(4), .width(16)) multiplexer_4 (
    .in0(alu_1_out), .in1(alu_1_out), .in2(alu_1_out), .in3(alu_1_out), .in4(alu_1_out), .in5(alu_1_out),
    .in6(alu_1_out), .in7(alu_1_out), .in9(multiplexer_5_out), .in10(or_2_out), .in11(shifter_1_out),
    .in15(register_1_q), .out(multiplexer_4_out), .sel(bitselector_4_out), .en(or_5_out));  // open: in8, in12, in13, in14
  Multiplexer #(.width(16)) multiplexer_5 (
    .in0(controlled_buffer_1_out), .in1(bitselector_2_out), .out(multiplexer_5_out), .sel(and_4_out));  // open: en
  BitSelector #(.width(7), .group(16)) bitselector_2 (.in(keyboard_1_data), .out(bitselector_2_out), .sel(1'b0));
  TTY tty_1 (.data(bitselector_1_out), .clk(and_1_out), .we(and_3_out), .clr(Clear));
  Keyboard keyboard_1 (.clk(and_1_out), .re(and_4_out), .clr(Clear), .data(keyboard_1_data));  // open: avail
  BitSelector #(.width(4), .group(3)) bitselector_3 (.in(bitselector_4_out), .out(bitselector_3_out), .sel(1'b0));
  BitSelector #(.width(16), .group(4)) bitselector_4 (.in(rom_1_data), .out(bitselector_4_out), .sel(2'b11));
  BitSelector #(.width(16), .group(4)) bitselector_5 (.in(rom_1_data), .out(bitselector_5_out), .sel(2'b01));
  BitSelector #(.width(16), .group(4)) bitselector_6 (.in(rom_1_data), .out(bitselector_6_out), .sel(2'b10));
  or or_1 (or_1_out, decoder_1_out8, decoder_1_out9);
  not not_3 (not_3_out, decoder_1_out8);
  BitSelector #(.width(16), .group(4)) bitselector_7 (.in(rom_1_data), .out(bitselector_7_out), .sel(2'b00));
  and and_5 (and_5_out, alu_1_bitbranch, decoder_1_out13);
  BitSelector #(.width(4), .group(16)) bitselector_8 (.in(bitselector_5_out), .out(bitselector_8_out), .sel(1'b0));
  BitSelector #(.width(4), .group(16)) bitselector_9 (.in(bitselector_7_out), .out(bitselector_9_out), .sel(1'b0));
  Decoder #(.select(4)) decoder_1 (
    .out0(decoder_1_out0), .out1(decoder_1_out1), .out2(decoder_1_out2), .out3(decoder_1_out3),
    .out4(decoder_1_out4), .out5(decoder_1_out5), .out6(decoder_1_out6), .out7(decoder_1_out7),
    .out8(decoder_1_out8), .out9(decoder_1_out9), .out10(decoder_1_out10), .out11(decoder_1_out11),
    .out12(decoder_1_out12), .out13(decoder_1_out13), .out14(decoder_1_out14), .out15(decoder_1_out15),
    .sel(bitselector_4_out));  // open: en
  Shifter #(.width(16)) shifter_1 (.in(or_2_out), .\dist (4'b1000), .out(shifter_1_out));
  Shifter #(.width(16)) shifter_2 (.in(bitselector_8_out), .\dist (4'b0100), .out(shifter_2_out));
  assign or_2_out = shifter_2_out | bitselector_9_out;  // OR_Gate or_2, 16 bits wide
  or or_3 (or_3_out, decoder_1_out0, decoder_1_out1, decoder_1_out2, decoder_1_out3, decoder_1_out4, decoder_1_out5, decoder_1_out6, decoder_1_out7);
  or or_4 (or_4_out, or_3_out, decoder_1_out9);
  or or_5 (or_5_out, or_4_out, decoder_1_out10, decoder_1_out11, decoder_1_out15);

  // Notes on the sheet:
  //   contents of rom_1 (hex, n*v repeats v):
  //   0 a1fe a2ff b3ff 431 532 9640 8056 c006
endmodule

module ALU (
  input  [15:0] A,
  input  [15:0] B,
  input  [2:0] S,
  input  Reloj,
  output [15:0] OUT,
  output BitBranch
);

  wire comparator_1_eq, comparator_1_lt, comparator_2_gt, or_2_out;
  wire [15:0] adder_1_out, and_1_out, bitselector_1_out, bitselector_2_out, or_1_out, shifter_1_out,
       subtractor_1_out, xor_1_out;

  Adder #(.width(16)) adder_1 (.a(A), .b(B), .out(adder_1_out));  // open: cin, cout
  Subtractor #(.width(16)) subtractor_1 (.a(A), .b(B), .out(subtractor_1_out));  // open: bin, bout
  assign and_1_out = A & B;  // AND_Gate and_1, 16 bits wide
  assign or_1_out = A | B;  // OR_Gate or_1, 16 bits wide
  assign xor_1_out = A ^ B;  // XOR_Gate xor_1, 16 bits wide
  Shifter #(.width(16)) shifter_1 (.in(A), .\dist (4'b0001), .out(shifter_1_out));
  Comparator #(.width(16)) comparator_1 (.a(A), .b(B), .eq(comparator_1_eq), .lt(comparator_1_lt));  // open: gt
  BitSelector #(.width(1), .group(16)) bitselector_1 (.in(comparator_1_eq), .out(bitselector_1_out), .sel(1'b0));
  BitSelector #(.width(1), .group(16)) bitselector_2 (.in(comparator_1_lt), .out(bitselector_2_out), .sel(1'b0));
  or or_2 (or_2_out, comparator_1_eq, comparator_1_lt);
  Multiplexer #(.select(3), .width(16), .enable("false")) multiplexer_1 (
    .in0(adder_1_out), .in1(subtractor_1_out), .in2(and_1_out), .in3(or_1_out), .in4(xor_1_out),
    .in5(shifter_1_out), .in6(bitselector_2_out), .in7(bitselector_1_out), .out(OUT), .sel(S));
  Comparator #(.width(3), .mode("unsigned")) comparator_2 (.a(S), .b(3'b101), .gt(comparator_2_gt));  // open: eq, lt
  Register #(.width(1)) register_1 (.D(or_2_out), .en(comparator_2_gt), .Q(BitBranch), .clk(Reloj));  // open: clr
endmodule

// REG
module REGS (
  input  [15:0] Rdest,
  input  [3:0] sRd,
  input  [3:0] sRs1,
  input  [3:0] sRs2,
  input  Enable,
  input  Clear,
  input  Reloj,
  output [15:0] Rsrc1,
  output [15:0] Rsrc2
);

  wire demultiplexer_2_out0, demultiplexer_2_out1, demultiplexer_2_out2, demultiplexer_2_out3,
       demultiplexer_2_out4, demultiplexer_2_out5, demultiplexer_2_out6, demultiplexer_2_out7,
       demultiplexer_2_out8, demultiplexer_2_out9, demultiplexer_2_out10, demultiplexer_2_out11,
       demultiplexer_2_out12, demultiplexer_2_out13, demultiplexer_2_out14, demultiplexer_2_out15;
  wire [15:0] demultiplexer_1_out1, demultiplexer_1_out2, demultiplexer_1_out3, demultiplexer_1_out4,
       demultiplexer_1_out5, demultiplexer_1_out6, demultiplexer_1_out7, demultiplexer_1_out8,
       demultiplexer_1_out9, demultiplexer_1_out10, demultiplexer_1_out11, demultiplexer_1_out12,
       demultiplexer_1_out13, demultiplexer_1_out14, demultiplexer_1_out15, R0_q, R1_q, R2_q, R3_q, R4_q,
       R5_q, R6_q, R7_q, R8_q, R9_q, R10_q, R11_q, R12_q, R13_q, R14_q, R15_q;

  Demultiplexer #(.select(4), .width(16), .enable("false")) demultiplexer_1 (
    .out1(demultiplexer_1_out1), .out2(demultiplexer_1_out2), .out3(demultiplexer_1_out3),
    .out4(demultiplexer_1_out4), .out5(demultiplexer_1_out5), .out6(demultiplexer_1_out6),
    .out7(demultiplexer_1_out7), .out8(demultiplexer_1_out8), .out9(demultiplexer_1_out9),
    .out10(demultiplexer_1_out10), .out11(demultiplexer_1_out11), .out12(demultiplexer_1_out12),
    .out13(demultiplexer_1_out13), .out14(demultiplexer_1_out14), .out15(demultiplexer_1_out15), .in(Rdest),
    .sel(sRd));  // open: out0
  Register #(.width(16)) R0 (.D({16{1'b0}}), .en(Enable), .Q(R0_q), .clk(demultiplexer_2_out0), .clr(Clear));
  Register #(.width(16)) R1 (.D(demultiplexer_1_out1), .en(Enable), .Q(R1_q), .clk(demultiplexer_2_out1), .clr(Clear));
  Register #(.width(16)) R2 (.D(demultiplexer_1_out2), .en(Enable), .Q(R2_q), .clk(demultiplexer_2_out2), .clr(Clear));
  Register #(.width(16)) R3 (.D(demultiplexer_1_out3), .en(Enable), .Q(R3_q), .clk(demultiplexer_2_out3), .clr(Clear));
  Register #(.width(16)) R4 (.D(demultiplexer_1_out4), .en(Enable), .Q(R4_q), .clk(demultiplexer_2_out4), .clr(Clear));
  Register #(.width(16)) R5 (.D(demultiplexer_1_out5), .en(Enable), .Q(R5_q), .clk(demultiplexer_2_out5), .clr(Clear));
  Register #(.width(16)) R6 (.D(demultiplexer_1_out6), .en(Enable), .Q(R6_q), .clk(demultiplexer_2_out6), .clr(Clear));
  Register #(.width(16)) R7 (.D(demultiplexer_1_out7), .en(Enable), .Q(R7_q), .clk(demultiplexer_2_out7), .clr(Clear));
  Register #(.width(16)) R8 (.D(demultiplexer_1_out8), .en(Enable), .Q(R8_q), .clk(demultiplexer_2_out8), .clr(Clear));
  Register #(.width(16)) R9 (.D(demultiplexer_1_out9), .en(Enable), .Q(R9_q), .clk(demultiplexer_2_out9), .clr(Clear));
  Register #(.width(16)) R10 (
    .D(demultiplexer_1_out10), .en(Enable), .Q(R10_q), .clk(demultiplexer_2_out10), .clr(Clear));
  Register #(.width(16)) R11 (
    .D(demultiplexer_1_out11), .en(Enable), .Q(R11_q), .clk(demultiplexer_2_out11), .clr(Clear));
  Register #(.width(16)) R12 (
    .D(demultiplexer_1_out12), .en(Enable), .Q(R12_q), .clk(demultiplexer_2_out12), .clr(Clear));
  Register #(.width(16)) R13 (
    .D(demultiplexer_1_out13), .en(Enable), .Q(R13_q), .clk(demultiplexer_2_out13), .clr(Clear));
  Register #(.width(16)) R14 (
    .D(demultiplexer_1_out14), .en(Enable), .Q(R14_q), .clk(demultiplexer_2_out14), .clr(Clear));
  Register #(.width(16)) R15 (
    .D(demultiplexer_1_out15), .en(Enable), .Q(R15_q), .clk(demultiplexer_2_out15), .clr(Clear));
  Demultiplexer #(.select(4), .enable("false")) demultiplexer_2 (
    .out0(demultiplexer_2_out0), .out1(demultiplexer_2_out1), .out2(demultiplexer_2_out2),
    .out3(demultiplexer_2_out3), .out4(demultiplexer_2_out4), .out5(demultiplexer_2_out5),
    .out6(demultiplexer_2_out6), .out7(demultiplexer_2_out7), .out8(demultiplexer_2_out8),
    .out9(demultiplexer_2_out9), .out10(demultiplexer_2_out10), .out11(demultiplexer_2_out11),
    .out12(demultiplexer_2_out12), .out13(demultiplexer_2_out13), .out14(demultiplexer_2_out14),
    .out15(demultiplexer_2_out15), .in(Reloj), .sel(sRd));
  Multiplexer #(.select(4), .width(16), .enable("false")) multiplexer_1 (
    .in0(R0_q), .in1(R1_q), .in2(R2_q), .in3(R3_q), .in4(R4_q), .in5(R5_q), .in6(R6_q), .in7(R7_q),
    .in8(R8_q), .in9(R9_q), .in10(R10_q), .in11(R11_q), .in12(R12_q), .in13(R13_q), .in14(R14_q),
    .in15(R15_q), .out(Rsrc1), .sel(sRs1));
  Multiplexer #(.select(4), .width(16), .enable("false")) multiplexer_2 (
    .in0(R0_q), .in1(R1_q), .in2(R2_q), .in3(R3_q), .in4(R4_q), .in5(R5_q), .in6(R6_q), .in7(R7_q),
    .in8(R8_q), .in9(R9_q), .in10(R10_q), .in11(R11_q), .in12(R12_q), .in13(R13_q), .in14(R14_q),
    .in15(R15_q), .out(Rsrc2), .sel(sRs2));
endmodule
